# Fritzing sketch breadboard_sketch_fritzing (saved by Fritzing 0.9.0b)
breadboards: 1

parts:
  S1 = Pushbutton [package="[THT]"]
  LED1 = LED - 5mm [color="Red (633nm)" package="5 mm [THT]"]
  Part1 = Arduino Uno (Rev3)
  R1 = Resistor [tolerance=±5% resistance=220 package=THT]
  R2 = Resistor [tolerance=±5% resistance=10k package=THT]

nets:
  N1: S1.Pin_1, S1.Pin_2, Part1.D2, R2.Pin_1
  N2: S1.Pin_3, S1.Pin_4, Part1.5V
  N3: LED1.cathode, R1.Pin_1
  N4: LED1.anode, Part1.D3_PWM
  N5: Part1.GND, R1.Pin_0, R2.Pin_0
